# Fritzing sketch ExternalInterrupts (saved by Fritzing 0.9.3b)
breadboards: 1

parts:
  IC1 = IC, DIP package, 16 pins [chip_label=MC14490P]
  S1 = Pushbutton [package="[THT]"]
  S2 = Pushbutton [package="[THT]"]
  Part1 = Arduino Uno (Rev3)
  LED1 = LED - 5mm [color="Red (633nm)" package="5 mm [THT]"]
  LED2 = LED - 5mm [color="Green (560nm)" package="5 mm [THT]"]
  R1 = Resistor [tolerance=±5% resistance=330 package=THT]
  R2 = Resistor [tolerance=±5% resistance=330 package=THT]
  C1 = Ceramic Capacitor [capacitance=1nF package="100 mil [THT, multilayer]"]

nets:
  N1: IC1.pin1, S1.Pin_3, S1.Pin_4
  N2: IC1.pin3, S2.Pin_3, S2.Pin_4
  N3: IC1.pin5, IC1.pin8, IC1.pin10, IC1.pin12, IC1.pin14, S1.Pin_1, S1.Pin_2, S2.Pin_1, S2.Pin_2, Part1.GND, R1.Pin_0, R2.Pin_0
  N4: IC1.pin7, C1.1
  N5: IC1.pin9, C1.0
  N6: IC1.pin13, Part1.D3_PWM
  N7: IC1.pin15, Part1.D2
  N8: IC1.pin16, Part1.5V
  N9: Part1.D8, LED2.anode
  N10: Part1.D13/SCK, LED1.anode
  N11: LED1.cathode, R2.Pin_1
  N12: LED2.cathode, R1.Pin_1

notes:
  ledFlash
  ledOnOff
  R1
  R2
  C1
  R1 = R2 = 330R
  C1 = 1nF (102)
  IC1
  IC1 = MC14490P
  SW1
  SW2
  SW1 = D2 = On
  SW2 = D3 = Off
  D8
  D2
  GND
  5V
  D13
  D3
