# Fritzing sketch Timer1Blink (saved by Fritzing 0.9.3b)
breadboards: 1

parts:
  Part1 = Arduino Uno (Rev3)
  LED1 = LED - 5mm [color="Red (633nm)" package="5 mm [THT]"]
  LED2 = LED - 5mm [color="Green (560nm)" package="5 mm [THT]"]
  R1 = Resistor [tolerance=±5% resistance=330 package=THT]
  R2 = Resistor [tolerance=±5% resistance=330 package=THT]

nets:
  N1: Part1.D8, LED2.anode
  N2: Part1.D13/SCK, LED1.anode
  N3: Part1.GND, R1.Pin_0, R2.Pin_0
  N4: LED1.cathode, R2.Pin_1
  N5: LED2.cathode, R1.Pin_1

notes:
  R1
  R2
  C1
  R1 = R2 = 330R
  GND
  D13
  D8
