# Fritzing sketch SPI_NO_LEDs_peripheral (saved by Fritzing 0.9.6b)

parts:
  Part1 = Arduino Uno (Rev3)
  Part2 = Arduino Uno (Rev3)

nets:
  N1: Part1.D10_PWM/SS, Part2.D10_PWM/SS
  N2: Part1.D11_PWM/MOSI, Part2.D11_PWM/MOSI
  N3: Part1.D12/MISO, Part2.D12/MISO
  N4: Part1.D13/SCK, Part2.D13/SCK
  5V: Part1.5V, Part2.5V
  GND: Part1.GND, Part2.GND

notes:
  5V
  Duemilanove - Controller
  Arduino Uno - Peripheral
  SCK
  MOSI
  MISO
  SS
  GND
