# Fritzing sketch ADCLED (saved by Fritzing 0.9.6b)
breadboards: 1

parts:
  Part1 = Arduino Uno (Rev3)
  R1 = Rotary Potentiometer (Small) [maximum_resistance=100kΩ package=THT]
  LED1 = LED - 5mm [color="Red (633nm)" current=0.030 package="5 mm [THT]"]
  R4 = Resistor [tolerance=±5% resistance=560 power=0.25 package=THT]

nets:
  N1: Part1.A0, R1.wiper
  N2: Part1.D9_PWM, R4.Pin_0
  N3: Part1.GND, R1.leg1, LED1.cathode
  N4: Part1.5V, R1.leg2
  N5: LED1.anode, R4.Pin_1

notes:
  R1 = R2 = 330R
  VR1 = 10K
  D9
  A0
  GND
  VCC 5V
