# Fritzing sketch TWI_Read (saved by Fritzing 0.9.3b)
breadboards: 1

parts:
  Part1 = Arduino Uno (Rev3)
  Part2 = Digital Temperature Sensor Breakout - TMP102
  R1 = Resistor [tolerance=±5% resistance=10k package=THT]
  R2 = Resistor [tolerance=±5% resistance=10k package=THT]

nets:
  N1: Part1.A4/SDA, Part2.SDA, R1.Pin_1
  N2: Part1.A5/SCL, Part2.SCL, R2.Pin_1
  N3: Part1.5V, Part2.V+, R1.Pin_0, R2.Pin_0
  GND: Part1.GND, Part2.GND

notes:
  C1
  GND
  5V
  R1 and R2 are 10K
  R1
  R2
  A4/SDA
  A5/SCL
