# Fritzing sketch RC_Debounce (saved by Fritzing 0.9.6b)
breadboards: 1

parts:
  R1 = Resistor [tolerance=±5% power=0.25 resistance=10k package=THT]
  R2 = Resistor [tolerance=±5% power=0.25 resistance=10k package=THT]
  C1 = Ceramic Capacitor [capacitance=0.1mF voltage=10V package="100 mil [THT, multilayer]"]
  S1 = Pushbutton [package="[THT]"]
  Part1 = Arduino Uno (Rev3)

nets:
  N1: R1.Pin_0, Part1.5V
  N2: R1.Pin_1, R2.Pin_0, S1.Pin_3, S1.Pin_4
  N3: R2.Pin_1, C1.0, Part1.D2
  N4: C1.1, S1.Pin_1, S1.Pin_2, Part1.GND

notes:
  D2
  VCC
  GND
  R1 = 10K
  R2 = 10K
  C1 = 100nF
  R1
  R2
  C1
